# Fritzing sketch blink_led_fritzing (saved by Fritzing 0.9.2b)
breadboards: 1

parts:
  Raspberry_Pi1 = Raspberry Pi B+
  LED1 = LED - 3mm [color="Red (633nm)" package="3 mm [THT]"]
  R1 = Resistor [tolerance=±5% resistance=220 package="0603 [SMD]"]

nets:
  N1: Raspberry_Pi1.GPIO17, R1.Pin_0
  N2: Raspberry_Pi1.GND, LED1.cathode
  N3: LED1.anode, R1.Pin_1
